# Fritzing sketch CO2 Sensor (saved by Fritzing 0.9.3b)
circuit board: 7cm x 5cm
breadboards: 1

parts:
  J6 = female pin header, 4 pins [form="♀ (female)"]
  J7 = female pin header, 4 pins [form="♀ (female)"]
  J8 = female pin header, 4 pins [form="♀ (female)"]
  U5 = atmega168 [package=dip]
  XTAL3 = Crystal [frequency="16 Mhz" package=THT]
  C8 = Ceramic Capacitor [capacitance=22pF rated_voltage=35V package="200 mil [THT, multilayer]"]
  C9 = Ceramic Capacitor [capacitance=22pF rated_voltage=35V package="200 mil [THT, multilayer]"]
  J9 = female pin header, 4 pins [form="♀ (female)"]
  LED2 = RGB LED - (4 legs) [package="5 mm [THT]"]
  R4 = Resistor [tolerance=±5% resistance=220 package=THT]
  R5 = Resistor [tolerance=±5% resistance=220 package=THT]
  R6 = Resistor [tolerance=±5% resistance=220 package=THT]
  J10 = female pin header, 1 pin [form="♀ (female)"]
  J11 = female pin header, 1 pin [form="♀ (female)"]
  J12 = female pin header, 1 pin [form="♀ (female)"]
  J13 = female pin header, 1 pin [form="♀ (female)"]
  R7 = Resistor [tolerance=±5% resistance=220 package=THT]

nets:
  N1: J6.pin1, J7.pin1, J8.pin1, U5.GND, C8.1, C9.0, J9.pin2, LED2.common_anode
  N2: J6.pin2, J7.pin2, J8.pin2, U5.A4
  N3: J6.pin3, J7.pin3, J8.pin3, U5.A5
  N4: J6.pin4, J7.pin4, J8.pin4, U5.VCC, U5.AREF, J9.pin1, J10.pin1, J11.pin1, J12.pin1, J13.pin1, R7.Pin_0
  N5: U5.RESET, R7.Pin_1
  N6: U5.XLAT1, XTAL3.pin_1, C8.0
  N7: U5.XLAT2, XTAL3.pin_0, C9.1
  N8: U5.D5_(PWM), R5.Pin_1
  N9: U5.D6_(PWM), R4.Pin_1
  N10: U5.D9_(PWM), R6.Pin_1
  N11: U5.A3, J9.pin4
  N12: LED2.red_cathode, R6.Pin_0
  N13: LED2.green_cathode, R4.Pin_0
  N14: LED2.blue_cathode, R5.Pin_0
