# Fritzing sketch Communication (saved by Fritzing 0.9.3b)
circuit board: 7cm x 5cm
breadboards: 1

parts:
  J2 = female pin header, 14 pins [form="♀ (female)"]
  J1 = female pin header, 14 pins [form="♀ (female)"]
  J3 = female pin header, 4 pins [form="♀ (female)"]
  J4 = female pin header, 4 pins [form="♀ (female)"]
  J5 = female pin header, 4 pins [form="♀ (female)"]
  LED1 = RGB LED - (4 legs) [package="5 mm [THT]"]
  R3 = Resistor [tolerance=±5% resistance=220 package=THT]
  R4 = Resistor [tolerance=±5% resistance=220 package=THT]
  R5 = Resistor [tolerance=±5% resistance=220 package=THT]
  J19 = female pin header, 1 pin [form="♀ (female)"]
  J21 = female pin header, 1 pin [form="♀ (female)"]
  Part2 = Adafruit nRF8001 Breakout [part_number="Adafruit #1697"]
  J35 = female pin header, 6 pins [form="♀ (female)"]
  J11 = female pin header, 2 pins [form="♀ (female)"]
  J9 = female pin header, 2 pins [form="♀ (female)"]
  J10 = female pin header, 2 pins [form="♀ (female)"]
  J36 = female pin header, 1 pin [form="♀ (female)"]
  J37 = female pin header, 1 pin [form="♀ (female)"]
  J38 = female pin header, 1 pin [form="♀ (female)"]
  J39 = female pin header, 1 pin [form="♀ (female)"]
  J40 = female pin header, 1 pin [form="♀ (female)"]
  J41 = female pin header, 1 pin [form="♀ (female)"]
  J42 = female pin header, 2 pins [form="♀ (female)"]
  J43 = female pin header, 2 pins [form="♀ (female)"]

nets:
  N1: J2.pin1, Part2.MISO
  N2: J2.pin2, Part2.MOSI
  N3: J2.pin3, Part2.REQN
  N4: J2.pin4, Part2.RDYN
  N5: J2.pin5, Part2.RESET
  N6: J2.pin9, J43.pin1
  N7: J2.pin10, J43.pin2
  N8: J2.pin14, J1.pin13, J3.pin4, J4.pin4, J5.pin4, LED1.common_anode, Part2.GND, J35.pin2, J11.pin1, J11.pin2, J36.pin1, J37.pin1
  N9: J1.pin1, J19.pin1, J21.pin1, Part2.SCK
  N10: J1.pin6, J3.pin3, J4.pin3, J5.pin3
  N11: J1.pin7, J3.pin2, J4.pin2, J5.pin2
  N12: J1.pin8, R3.Pin_1
  N13: J1.pin9, R4.Pin_1
  N14: J1.pin10, R5.Pin_1
  N15: J1.pin11, J10.pin2, J40.pin1, J41.pin1
  N16: J1.pin12, Part2.VIN, J35.pin1, J38.pin1, J39.pin1
  N17: J1.pin14, J3.pin1, J4.pin1, J5.pin1
  N18: LED1.red_cathode, R5.Pin_0
  N19: LED1.green_cathode, R4.Pin_0
  N20: LED1.blue_cathode, R3.Pin_0
  N21: J35.pin3, J42.pin1
  N22: J35.pin4, J42.pin2
  N23: J35.pin5, J10.pin1
  N24: J35.pin6, J9.pin1

custom parts:
  Adafruit nRF8001 Breakout: Our Adafruit Bluefruit LE (Bluetooth Smart, Bluetooth Low Energy, Bluetooth 4.0) nRF8001 Breakout allows you to establish an easy to use wireless link between your Arduino and any compatible iOS or Android (4.3+) device. It works by simulating a UART device beneath the surface, sending ASCII data back and forth between the devices, letting you decide what data to send and what to do with it on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
