# Fritzing sketch Core (saved by Fritzing 0.9.3b)
circuit board: 7cm x 5cm
breadboards: 1

parts:
  J2 = female pin header, 14 pins [form="♀ (female)"]
  J1 = female pin header, 14 pins [form="♀ (female)"]
  J3 = female pin header, 4 pins [form="♀ (female)"]
  J4 = female pin header, 4 pins [form="♀ (female)"]
  J5 = female pin header, 4 pins [form="♀ (female)"]
  J9 = female pin header, 4 pins [form="♀ (female)"]
  J10 = female pin header, 4 pins [form="♀ (female)"]
  J11 = female pin header, 4 pins [form="♀ (female)"]
  LED1 = RGB LED - (4 legs) [package="5 mm [THT]"]
  J16 = Power Jack [package=power_jack_slot]
  C10 = Electrolytic Capacitor [capacitance=10µF rated_voltage=35V package="100 mil [THT, electrolytic]"]
  C11 = Electrolytic Capacitor [capacitance=10µF rated_voltage=35V package="100 mil [THT, electrolytic]"]
  U4 = Voltage Regulator - 5V [package="TO220 [THT]"]
  R1 = Resistor [tolerance=±5% resistance=220 package=THT]
  R2 = Resistor [tolerance=±5% resistance=220 package=THT]
  R3 = Resistor [tolerance=±5% resistance=220 package=THT]
  R4 = Resistor [tolerance=±5% resistance=220 package=THT]
  R5 = Resistor [tolerance=±5% resistance=220 package=THT]
  J17 = female pin header, 1 pin [form="♀ (female)"]
  J18 = female pin header, 1 pin [form="♀ (female)"]
  Part1 = Adafruit MicroSD card breakout board [part_number="Adafruit #254"]
  J19 = female pin header, 1 pin [form="♀ (female)"]
  J21 = female pin header, 1 pin [form="♀ (female)"]
  J23 = female pin header, 1 pin [form="♀ (female)"]
  J24 = female pin header, 1 pin [form="♀ (female)"]
  J25 = female pin header, 1 pin [form="♀ (female)"]
  J26 = female pin header, 1 pin [form="♀ (female)"]
  J27 = female pin header, 1 pin [form="♀ (female)"]
  J28 = female pin header, 1 pin [form="♀ (female)"]
  J29 = female pin header, 1 pin [form="♀ (female)"]
  J30 = female pin header, 1 pin [form="♀ (female)"]
  J31 = female pin header, 1 pin [form="♀ (female)"]
  J32 = female pin header, 1 pin [form="♀ (female)"]
  J33 = female pin header, 1 pin [form="♀ (female)"]
  J34 = female pin header, 1 pin [form="♀ (female)"]

nets:
  N1: J2.pin1, Part1.DO
  N2: J2.pin2, Part1.DI
  N3: J2.pin3, Part1.CS
  N4: J1.pin1, Part1.CLK, J19.pin1, J21.pin1
  N5: J1.pin6, J3.pin3, J4.pin3, J5.pin3, J9.pin2, J10.pin2, J11.pin2, R1.Pin_1
  N6: J1.pin7, J3.pin2, J4.pin2, J5.pin2, J9.pin3, J10.pin3, J11.pin3, R2.Pin_1, J31.pin1, J32.pin1
  N7: J1.pin8, R3.Pin_1
  N8: J1.pin9, R4.Pin_1
  N9: J1.pin10, R5.Pin_1
  N10: J1.pin12, R1.Pin_0, R2.Pin_0, J33.pin1, J34.pin1
  GND: J1.pin13, J3.pin4, J4.pin4, J5.pin4, J9.pin1, J10.pin1, J11.pin1, LED1.common_anode, J16.GNDBREAK, J16.GND, C10.-, C11.-, U4.GND, Part1.GND, J27.pin1, J28.pin1, J29.pin1, J30.pin1
  N11: J1.pin14, J3.pin1, J4.pin1, J5.pin1, J9.pin4, J10.pin4, J11.pin4, C11.+, U4.output_voltage, J17.pin1, J18.pin1, Part1.VCC, J23.pin1, J24.pin1, J25.pin1, J26.pin1
  N12: LED1.red_cathode, R5.Pin_0
  N13: LED1.green_cathode, R4.Pin_0
  N14: LED1.blue_cathode, R3.Pin_0
  N15: J16.PWR, C10.+, U4.input_voltage

custom parts:
  Adafruit MicroSD card breakout board: Not just a simple breakout board, this microSD adapter goes the extra mile - designed for ease of use. Onboard 5v->3v regulator provides 150mA for power-hungry cards 3v level shifting means you can use this with ease on either 3v or 5v systems Uses a proper level shifting chip, not resistors: less problems, and faster read/write access Use 3 or 4 digital pins to read and write 2Gb+ of storage!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
